// Logisim project CLG.circ as structural Verilog: 1 circuit, main circuit main
module main (
  input  G0,
  input  P0,
  input  C0,
  input  G1,
  input  P1,
  output C1,
  output C2
);

  wire and_1_out, and_2_out, and_3_out;

  and and_1 (and_1_out, P0, C0);
  and and_2 (and_2_out, P1, P0, C0);
  and and_3 (and_3_out, P1, G0);
  or or_1 (C1, and_1_out, G0);
  or or_2 (C2, and_2_out, and_3_out, G1);
endmodule
