// Logisim project 4-bit_decre.circ as structural Verilog: 1 circuit, main circuit main
module main (
  input  in_1,
  input  in_2,
  input  in_3,
  input  in_4,
  input  in_5,
  output out_6,
  output out_7,
  output out_8,
  output out_9,
  output out_10
);

  wire main_2_cout, main_3_cout, main_4_cout;

  FULLADDER_main main_1 (.A(in_1), .B(1'b1), .Cin(main_2_cout), .S(out_7), .Cout(out_6));
  FULLADDER_main main_2 (.A(in_2), .B(1'b1), .Cin(main_3_cout), .S(out_8), .Cout(main_2_cout));
  FULLADDER_main main_3 (.A(in_3), .B(1'b1), .Cin(main_4_cout), .S(out_9), .Cout(main_3_cout));
  FULLADDER_main main_4 (.A(in_4), .B(1'b1), .Cin(in_5), .S(out_10), .Cout(main_4_cout));
endmodule
