// Logisim project Adder_Sub_Comp_Unit.circ as structural Verilog: 1 circuit, main circuit main
module main (
  input  in_1,
  input  in_2,
  input  in_3,
  input  in_4,
  input  in_5,
  input  in_6,
  input  in_7,
  input  in_8,
  input  in_9,
  output out_10,
  output out_11,
  output out_12,
  output out_13,
  output out_14
);

  wire main_2_cout, main_3_cout, main_4_cout, xor_1_out, xor_2_out, xor_3_out, xor_4_out;

  xor xor_1 (xor_1_out, in_1, in_9);
  FULLADDER_main main_1 (.A(in_5), .B(xor_1_out), .Cin(main_2_cout), .S(out_11), .Cout(out_10));
  xor xor_2 (xor_2_out, in_2, in_9);
  FULLADDER_main main_2 (.A(in_6), .B(xor_2_out), .Cin(main_3_cout), .S(out_12), .Cout(main_2_cout));
  xor xor_3 (xor_3_out, in_3, in_9);
  FULLADDER_main main_3 (.A(in_7), .B(xor_3_out), .Cin(main_4_cout), .S(out_13), .Cout(main_3_cout));
  xor xor_4 (xor_4_out, in_4, in_9);
  FULLADDER_main main_4 (.A(in_8), .B(xor_4_out), .Cin(in_9), .S(out_14), .Cout(main_4_cout));
endmodule
