// Logisim project Arithmatic_Unit2.circ as structural Verilog: 1 circuit, main circuit main
module main (
  input  Cin,
  input  A0,
  input  [1:0] B0,
  input  in_4,
  input  A1,
  input  B1,
  input  B2,
  input  A2,
  input  B3,
  input  A3,
  output R0,
  output R1,
  output R2,
  output R3,
  output Cout
);

  wire multiplexer_1_out, multiplexer_2_out, multiplexer_3_out, multiplexer_4_out, not_1_out, not_2_out,
       not_3_out, not_4_out;

  not not_1 (not_1_out, in_4);
  not not_2 (not_2_out, B1);
  not not_3 (not_3_out, B2);
  not not_4 (not_4_out, B3);
  Multiplexer #(.select(2)) multiplexer_1 (
    .in0(in_4), .in1(not_1_out), .in2(1'b1), .in3(1'b0), .out(multiplexer_1_out), .sel(B0), .en(1'b1));
  Multiplexer #(.select(2)) multiplexer_2 (
    .in0(B1), .in1(not_2_out), .in2(1'b1), .in3(1'b0), .out(multiplexer_2_out), .sel(B0), .en(1'b1));
  Multiplexer #(.select(2)) multiplexer_3 (
    .in0(B2), .in1(not_3_out), .in2(1'b1), .in3(1'b0), .out(multiplexer_3_out), .sel(B0), .en(1'b1));
  Multiplexer #(.select(2)) multiplexer_4 (
    .in0(B3), .in1(not_4_out), .in2(1'b1), .in3(1'b0), .out(multiplexer_4_out), .sel(B0), .en(1'b1));
  RIPPLE_CARRY_ADDER_main main_1 (
    .Cout(Cout), .Cin(Cin), .in_1(multiplexer_4_out), .A3(A3), .B2(multiplexer_3_out), .A2(A2),
    .B1(multiplexer_2_out), .A1(A1), .B0(multiplexer_1_out), .A0(A0), .out_11(R3), .out_12(R2), .out_13(R1),
    .S0(R0));
endmodule
