// Logisim project CFA.circ as structural Verilog: 1 circuit, main circuit main
module main (
  input  A,
  input  B,
  input  C,
  output P,
  output S,
  output G
);

  and and_1 (G, A, B);
  xor xor_1 (P, A, B);
  xor xor_2 (S, P, C);
endmodule
