// Logisim project Carry look Ahead Adder.circ as structural Verilog: 1 circuit, main circuit main
module main (
  input  in_1,
  input  in_2,
  input  in_3,
  input  in_4,
  input  in_5,
  output S0,
  output S1,
  output C_out
);

  wire FA1_g, FA1_p, FA2_g, FA2_p, main_1_c1;

  CFA_main FA2 (.A(in_2), .B(in_1), .C(main_1_c1), .P(FA2_p), .S(S1), .G(FA2_g));
  CLG_main main_1 (.C1(main_1_c1), .C2(C_out), .G0(FA1_g), .P0(FA1_p), .C0(in_5), .G1(FA2_g), .P1(FA2_p));
  CFA_main FA1 (.A(in_3), .B(in_4), .C(in_5), .P(FA1_p), .S(S0), .G(FA1_g));
endmodule
