// Logisim project RIPPLE_CARRY_ADDER.circ as structural Verilog: 1 circuit, main circuit main
module main (
  input  in_1,
  input  A3,
  input  B2,
  input  A2,
  input  B1,
  input  A1,
  input  B0,
  input  A0,
  input  Cin,
  output Cout,
  output out_11,
  output out_12,
  output out_13,
  output S0
);

  wire main_1_p5, main_2_p5, main_3_p5;

  // FULLADDER_TUHINGHOSH_main main_1: pin names not known; wires that end beside it: Cout, in_1, out_11, A3, main_1_p5
  // FULLADDER_TUHINGHOSH_main main_2: pin names not known; wires that end beside it: main_1_p5, B2, out_12, A2, main_2_p5
  // FULLADDER_TUHINGHOSH_main main_3: pin names not known; wires that end beside it: main_2_p5, B1, out_13, A1, main_3_p5
  // FULLADDER_TUHINGHOSH_main main_4: pin names not known; wires that end beside it: main_3_p5, B0, S0, A0, Cin

  // Notes on the sheet:
  //   B3
  //   S3
  //   C2
  //   S2
  //   C1
  //   S1
  //   C0
endmodule
