// Logisim project twoRam.circ as structural Verilog: 1 circuit, main circuit main
module main (
  input  [6:0] in_1,
  input  [7:0] in_2,
  input  in_3,
  input  in_4,
  input  in_5,
  input  in_6,
  output [7:0] out_7
);

  wire clock_1_out, clock_2_out, not_1_out;

  Clock clock_1 (.out(clock_1_out));
  Clock clock_2 (.out(clock_2_out));
  not not_1 (not_1_out, 1'b1);
  RAM #(.addrWidth(7), .bus("separate")) ram_1 (
    .addr(in_1), .din(in_2), .data(out_7), .str(in_4), .sel(1'b1), .clk(clock_1_out), .ld(in_5), .clr(in_3));
  RAM #(.addrWidth(7), .bus("separate")) ram_2 (
    .addr(in_1), .din(in_2), .data(out_7), .str(in_4), .sel(not_1_out), .clk(clock_2_out), .ld(in_5),
    .clr(in_6));

  // Notes on the sheet:
  //   RAM2
  //   RAM1
endmodule
